// Logisim project 1.circ as structural Verilog: 1 circuit, main circuit main
module main (
  input  [31:0] x,
  input  [31:0] Y,
  input  [1:0] AluOp,
  input  [4:0] ShiftNum,
  input  in_5,
  input  in_6,
  output [31:0] out_7,
  output [31:0] out_8
);

  wire CarryOut, comparator_1_eq;
  wire [31:0] adder_1_out, HighBits, multiplexer_1_out, multiplier_1_out, shifter_1_out;

  // Probe on x
  Adder #(.width(32)) adder_1 (.a(x), .b(Y), .out(adder_1_out), .cout(CarryOut));  // open: cin
  Multiplier #(.width(32)) multiplier_1 (.a(x), .b(Y), .out(multiplier_1_out), .cout(HighBits));  // open: cin
  Comparator #(.width(32), .mode("twosComplement")) comparator_1 (.a(x), .b(Y), .eq(comparator_1_eq));  // open: gt, lt
  Shifter #(.width(32), .shift("lr")) shifter_1 (.in(x), .\dist (ShiftNum), .out(shifter_1_out));
  // Probe on Y
  Multiplexer #(.select(2), .width(32), .disabled("Z"), .enable("false")) multiplexer_1 (
    .in0(adder_1_out), .in1(multiplier_1_out), .in3(shifter_1_out), .out(multiplexer_1_out), .sel(AluOp));  // open: in2
  // Probe on out_7
  // Probe on out_8
  Multiplexer #(.select(2), .width(32), .disabled("Z"), .enable("false")) multiplexer_2 (
    .in0(multiplexer_1_out), .in1(multiplexer_1_out), .in2({32{1'b0}}), .in3(multiplexer_1_out), .out(out_7),
    .sel(AluOp));
  Multiplexer #(.select(2), .width(32), .disabled("Z"), .enable("false")) multiplexer_3 (
    .in0({32{1'b0}}), .in1(HighBits), .in2({32{1'b0}}), .in3({32{1'b0}}), .out(out_8), .sel(AluOp));
  Multiplexer #(.select(2), .width(1), .disabled("Z"), .enable("false")) multiplexer_4 (
    .in0(CarryOut), .in1(1'b0), .in2(1'b0), .in3(1'b0), .out(in_5), .sel(AluOp));
  Multiplexer #(.select(2), .width(1), .disabled("Z"), .enable("false")) multiplexer_5 (
    .in0(1'b0), .in1(1'b0), .in2(comparator_1_eq), .in3(1'b0), .out(in_6), .sel(AluOp));
  // Probe on out_7
  // Probe on out_8
  // Probe on in_5
  // Probe on in_6

  // Other names for the same wires on the sheet: Carry = in_5; equal = in_6; R[31:0] = out_7; R2[31:0] = out_8
endmodule
